// Logisim project IT012_Lab02_20522132.circ as structural Verilog
module Warmup (
  input  [7:0] A,
  input  [7:0] B,
  output [7:0] S
);

  Adder adder_1 (.a(A), .b(B), .out(S));  // open: cin, cout
  // Probe on S
endmodule

module FA (
  input  A,
  input  B,
  input  cin,
  output cout,
  output S
);

  wire and_1_out, and_2_out, xor_1_out;

  and and_1 (and_1_out, A, B);
  xor xor_1 (xor_1_out, A, B);
  and and_2 (and_2_out, xor_1_out, cin);
  xor xor_2 (S, xor_1_out, cin);
  or or_1 (cout, and_1_out, and_2_out);
endmodule

module ADDSUB4 (
  input  [3:0] A,
  input  [3:0] B,
  input  SUB,
  output C,
  output C3,
  output [3:0] S,
  output C2,
  output C1
);

  wire xor_1_out, xor_2_out, xor_3_out, xor_4_out;

  xor xor_1 (xor_1_out, B[3], SUB);
  xor xor_2 (xor_2_out, B[2], SUB);
  xor xor_3 (xor_3_out, B[1], SUB);
  xor xor_4 (xor_4_out, B[0], SUB);
  FA fa_1 (.A(A[0]), .B(xor_4_out), .cin(SUB), .cout(C1), .S(S[0]));
  FA fa_2 (.A(A[2]), .B(xor_2_out), .cin(C2), .cout(C3), .S(S[2]));
  FA fa_3 (.A(A[1]), .B(xor_3_out), .cin(C1), .cout(C2), .S(S[1]));
  FA fa_4 (.A(A[3]), .B(xor_1_out), .cin(C3), .cout(C), .S(S[3]));
endmodule

module ALU8 (
  input  [7:0] A,
  input  [7:0] B,
  input  [2:0] OP,
  output LT,
  output [7:0] R,
  output Z
);

  wire and_2_out, and_3_out, not_2_out, xnor_1_out;
  wire [7:0] adder_1_out, adder_2_out, and_1_out, multiplexer_1_out, multiplexer_2_out, not_1_out, or_1_out,
       subtractor_1_out, subtractor_2_out, xor_1_out;

  Adder adder_1 (.a(A), .b(B), .out(adder_1_out));  // open: cin, cout
  Adder adder_2 (.a(A), .b(8'h1), .out(adder_2_out));  // open: cin, cout
  Subtractor subtractor_1 (.a(A), .b(B), .out(subtractor_1_out));  // open: bin, bout
  Subtractor subtractor_2 (.a(A), .b(8'h1), .out(subtractor_2_out));  // open: bin, bout
  assign and_1_out = A & B;  // AND_Gate and_1, 8 bits wide
  assign or_1_out = A | B;  // OR_Gate or_1, 8 bits wide
  assign not_1_out = ~A;  // NOT_Gate not_1, 8 bits wide
  assign xor_1_out = A ^ B;  // XOR_Gate xor_1, 8 bits wide
  Multiplexer #(.select(2), .width(8), .enable("false")) multiplexer_1 (
    .in0(adder_1_out), .in1(adder_2_out), .in2(subtractor_1_out), .in3(subtractor_2_out),
    .out(multiplexer_1_out), .sel(OP[1:0]));
  Multiplexer #(.select(2), .width(8), .enable("false")) multiplexer_2 (
    .in0(and_1_out), .in1(or_1_out), .in2(not_1_out), .in3(xor_1_out), .out(multiplexer_2_out), .sel(OP[1:0]));
  Multiplexer #(.width(8), .enable("false")) multiplexer_3 (
    .in0(multiplexer_1_out), .in1(multiplexer_2_out), .out(R), .sel(OP[2]));
  not not_2 (not_2_out, B[7]);
  xnor xnor_1 (xnor_1_out, A[7], B[7]);
  and and_2 (and_2_out, A[7], not_2_out);
  and and_3 (and_3_out, xnor_1_out, R[7]);
  nor nor_1 (Z, R[7], R[6], R[5], R[4], R[3], R[2], R[1], R[0]);
  or or_2 (LT, and_2_out, and_3_out);
endmodule

module DLATCH (
  input  D,
  input  E,
  output Q
);

  Multiplexer #(.enable("false")) multiplexer_1 (.in0(Q), .in1(D), .out(Q), .sel(E));
endmodule

module TN3 (
  input  D,
  input  CLK,
  output Q2,
  output Q1,
  output Q1_2,
  output Q2_2,
  output Q2_3,
  output Q1_3
);

  D_Flip_Flop d_ff_1 (.clk(CLK), .D(D), .Q(Q2));  // open: Qn, preset, en, reset
  DLATCH dlatch_1 (.D(D), .E(CLK), .Q(Q1));
  DLATCH dlatch_2 (.D(D), .E(CLK), .Q(Q1_2));
  D_Flip_Flop d_ff_2 (.clk(CLK), .D(D), .Q(Q1_3));  // open: Qn, preset, en, reset
  DLATCH dlatch_3 (.D(Q1_2), .E(CLK), .Q(Q2_2));
  D_Flip_Flop d_ff_3 (.clk(CLK), .D(Q1_3), .Q(Q2_3));  // open: Qn, preset, en, reset
endmodule

module REGFILE (
  input  [7:0] DIN,
  input  CLK,
  input  [1:0] RA,
  input  WE,
  input  [1:0] RD,
  input  [1:0] RB,
  output [7:0] R0,
  output [7:0] QA,
  output [7:0] R1,
  output [7:0] R2,
  output [7:0] QB,
  output [7:0] R3
);

  wire decoder_1_out0, decoder_1_out1, decoder_1_out2, decoder_1_out3;

  Decoder #(.select(2), .disabled(0)) decoder_1 (
    .out0(decoder_1_out0), .out1(decoder_1_out1), .out2(decoder_1_out2), .out3(decoder_1_out3), .sel(RD),
    .en(WE));
  Register register_1 (.D(DIN), .en(decoder_1_out0), .Q(R0), .clk(CLK));  // open: clr
  Register register_2 (.D(DIN), .en(decoder_1_out1), .Q(R1), .clk(CLK));  // open: clr
  Register register_3 (.D(DIN), .en(decoder_1_out2), .Q(R2), .clk(CLK));  // open: clr
  Register register_4 (.D(DIN), .en(decoder_1_out3), .Q(R3), .clk(CLK));  // open: clr
  Multiplexer #(.select(2), .width(8), .enable("false")) multiplexer_1 (
    .in0(R0), .in1(R1), .in2(R2), .in3(R3), .out(QA), .sel(RA));
  Multiplexer #(.select(2), .width(8), .enable("false")) multiplexer_2 (
    .in0(R0), .in1(R1), .in2(R2), .in3(R3), .out(QB), .sel(RB));
endmodule

module DATAPATH (
  input  [1:0] RA,
  input  CLK,
  input  WE,
  input  [1:0] RD,
  input  [1:0] RB,
  input  [2:0] OP,
  input  [7:0] IMM,
  input  SRC,
  output [7:0] R0,
  output [7:0] R1,
  output [7:0] R2,
  output [7:0] R3,
  output [7:0] R,
  output Z
);

  wire [7:0] multiplexer_1_out, regfile_1_qa, regfile_1_qb;

  REGFILE regfile_1 (
    .DIN(multiplexer_1_out), .CLK(CLK), .RA(RA), .WE(WE), .RD(RD), .RB(RB), .R0(R0), .QA(regfile_1_qa),
    .R1(R1), .R2(R2), .QB(regfile_1_qb), .R3(R3));
  ALU8 alu8_1 (.A(regfile_1_qa), .B(regfile_1_qb), .OP(OP), .R(R), .Z(Z));  // open: LT
  Multiplexer #(.width(8), .enable("false")) multiplexer_1 (.in0(R), .in1(IMM), .out(multiplexer_1_out), .sel(SRC));
endmodule
